# Fritzing sketch digiDryerMonLayout (saved by Fritzing 0.9.3b)
breadboards: 1

parts:
  WeMos_D1_Mini1 = WeMos D1 Mini  # not connected
  J1 = screw terminal, 3 pins
  R1 = Resistor [tolerance=±5% resistance=10k package="1206 [SMD]"]
  R2 = Resistor [tolerance=±5% resistance=10k package="1206 [SMD]"]
  C2 = Electrolytic Capacitor [capacitance=1μF package="0405 [SMD, electrolytic]"]

nets:
  N1: J1.pin1, R1.Pin_1, R2.Pin_1, C2.+
  N2: R2.Pin_0, C2.-
